// Logisim project DL LAB 1.circ as structural Verilog: 1 circuit, main circuit main
module main (
  input  A,
  input  B,
  input  A_2,
  input  B_2,
  input  A_3,
  input  B_3,
  input  A_4,
  input  B_4,
  input  A_5,
  output Y_AB,
  output Y_A_prime_B_AB_prime,
  output Y_A_B,
  output Y_AB_A_prime_B,
  output Y_A
);

  and AND (Y_AB, A, B);
  or OR (Y_A_B, A_3, B_3);
  not NOT (Y_A, A_5);
  xor XOR (Y_A_prime_B_AB_prime, A_2, B_2);
  xnor XNOR (Y_AB_A_prime_B, A_4, B_4);
endmodule
