// Logisim project DL LAB 2.circ as structural Verilog: 1 circuit, main circuit main
module main (
  input  A,
  input  A_2,
  input  B,
  input  A_3,
  input  B_2,
  output Y1,
  output Y2,
  output Y3
);

  wire nand_2_out, nand_3_out, nand_4_out;

  nand nand_1 (Y1, A, A);
  nand nand_2 (nand_2_out, A_2, B);
  nand nand_3 (nand_3_out, A_3, A_3);
  nand nand_4 (nand_4_out, B_2, B_2);
  nand nand_5 (Y3, nand_3_out, nand_4_out);
  nand nand_6 (Y2, nand_2_out, nand_2_out);

  // Notes on the sheet:
  //   1 . NOT using NAND
  //   2 .AND using NAND
  //   3 .OR using NAND
endmodule
